# Fritzing sketch IoT_Smart_Plant (saved by Fritzing 0.9.3b)
breadboards: 1

parts:
  Part1 = ESP32-S3 WROOM [package=ESP32]
  WATER_PUMP1 = water pump/motor  # not connected
  Mod1 = KY-015 Temperature & Humidity Sensor Module [package="Breakout board"]
  Εξάρτημα1 = Soil Moisture Sensor
  YwRobot_Power_Supply1 = YwRobot Breadboard Power Supply [part_number=545043]
  M1 = 1 chan 5v relay module

nets:
  N1: Part1.14, M1.pin_3
  N2: Part1.11, Mod1.Vin
  N3: Part1.1, Εξάρτημα1.SIG
  N4: Mod1.S, Εξάρτημα1.VCC, YwRobot_Power_Supply1.VCC#5, YwRobot_Power_Supply1.VCC#6, M1.pin_1
  N5: Mod1.-, Εξάρτημα1.GND, YwRobot_Power_Supply1.GND#11, YwRobot_Power_Supply1.GND#12, M1.pin_2
  N6: YwRobot_Power_Supply1.VCC#9, YwRobot_Power_Supply1.VCC#10, M1.pin_5
  N7: YwRobot_Power_Supply1.GND#13, YwRobot_Power_Supply1.GND#14

custom parts:
  ESP32-S3 WROOM: FREENOVE ESP32-S3 WROOM-1 2.4 GHz Wi-Fi (802.11b/g/n) and Bluetooth® 5 (LE )module Built around ESP32-S3 series of SoCs, Xtensa® dual-core32-bit LX7 microprocessor Flash up to16MB, PSRAM up to 8 MB 36 GPIOs, rich set of peripherals On-board PCB antenna
  water pump/motor: WATER PUMP BY ARDUBLOCKTR
  KY-015 Temperature & Humidity Sensor Module: KY-015 temperature and humidity sensor module, provides a low-latency serial interface to measure humidity and temperature.
  YwRobot Breadboard Power Supply: The YwRobot Breadboard Power Supply (MB-V2) has two power rails; they can be 5V or 3V3. Power to the module can be provided through the female USB socket or through the A10 (female) 2.1mm power jack.
  1 chan 5v relay module: 1 Channel 5V Relay Module Board Shield with Optocoupler Support High and Low Level Trigger for Arduino.
